# Fritzing sketch lora_sensor_schem (saved by Fritzing 0.9.9b)
breadboards: 1

parts:
  Bauteil1 = Arduino Nano (Rev3.0) (ICSP)
  DHT1 = DHT22 Humidity and Temperature Sensor
  R1 = Resistor [tolerance=±5% resistance=220 package="2512 [SMD]"]
  RFM95W1 = RFM95W LoRa Module

nets:
  N1: Bauteil1.D2, RFM95W1.14_DIO0
  N2: Bauteil1.D3, RFM95W1.15_DIO1
  N3: Bauteil1.D4, RFM95W1.16_DIO2
  N4: Bauteil1.D5, RFM95W1.6_RESET
  N5: Bauteil1.D6, DHT1.DATA, R1.Pin_0
  N6: Bauteil1.D10, RFM95W1.5_NSS_(CS)
  N7: Bauteil1.D11/MOSI, RFM95W1.3_MOSI
  N8: Bauteil1.D12/MISO, RFM95W1.2_MISO
  3V3: Bauteil1.3V3, DHT1.VDD, R1.Pin_1, RFM95W1.13_3.3V
  N9: Bauteil1.D13/SCK, RFM95W1.4_SCK
  N10: DHT1.GND, RFM95W1.1_GND, RFM95W1.8_GND

custom parts:
  RFM95W LoRa Module: RF Transceiver by Hope RF. Well supported Arduino libraries are available. This Low Power Long Range Transceiver Module for the frequencies 868MHz and 915MHz and it is also available in other versions.
